# Fritzing sketch potentionmeter fritzing connection (saved by Fritzing 0.9.3b)
breadboards: 1

parts:
  Part1 = Arduino Nano (Rev3.0)
  U1 = POT [package=pot_alpha_rv16af-20]

nets:
  N1: Part1.GND, U1.A
  N2: Part1.5V, U1.E
  N3: Part1.A3, U1.S
